// Logisim project AnigmaLogisim.circ as structural Verilog: 12 circuits, main circuit main
module main (
  input  [4:0] in_1,
  input  in_2,
  output [4:0] out_3,
  output [4:0] out_4
);

  wire A_out, B_out, C_out, D_out, E_out, F_out, G_out, H_out, I_out, J_out, K_out, keyboard_1_out_27,
       keyboard_1_out_28, keyboard_1_out_29, keyboard_1_out_30, keyboard_1_out_31, keyboard_1_out_32, L_out,
       M_out, mainboard_1_out_9, mainboard_1_out_10, mainboard_1_out_11, mainboard_1_out_12,
       mainboard_1_out_13, N_out, not_1_out, O_out, output_1_a, output_1_b, output_1_c, output_1_d,
       output_1_e, output_1_f, output_1_g, output_1_h, output_1_i, output_1_j, output_1_k, output_1_l,
       output_1_m, output_1_n, output_1_o, output_1_p, output_1_q, output_1_r, output_1_s, output_1_t,
       output_1_u, output_1_v, output_1_w, output_1_x, output_1_y, output_1_z, P_out, Q_out, R_out, S_out,
       T_out, U_out, V_out, W_out, X_out, Y_out, Z_out;

  Button Q (.out(Q_out));
  Keyboard keyboard_1 (
    .out_27(keyboard_1_out_27), .Q(Q_out), .A(A_out), .Z(Z_out), .W(W_out), .S(S_out), .X(X_out), .E(E_out),
    .D(D_out), .C(C_out), .R(R_out), .F(F_out), .V(V_out), .T(T_out), .G(G_out), .B(B_out), .Y(Y_out),
    .H(H_out), .N(N_out), .U(U_out), .J(J_out), .M(M_out), .I(I_out), .K(K_out), .O(O_out), .L(L_out),
    .P(P_out), .out_28(keyboard_1_out_28), .out_29(keyboard_1_out_29), .out_30(keyboard_1_out_30),
    .out_31(keyboard_1_out_31), .out_32(keyboard_1_out_32));
  Button W (.out(W_out));
  Button E (.out(E_out));
  Button A (.out(A_out));
  Button D (.out(D_out));
  Button S (.out(S_out));
  Button X (.out(X_out));
  Button C (.out(C_out));
  Button Z (.out(Z_out));
  not not_1 (not_1_out, keyboard_1_out_27);
  Button R (.out(R_out));
  Button T (.out(T_out));
  Button Y (.out(Y_out));
  Button F (.out(F_out));
  Button G (.out(G_out));
  Button H (.out(H_out));
  Button V (.out(V_out));
  Button B (.out(B_out));
  MainBoard mainboard_1 (
    .in_1(keyboard_1_out_28), .in_2(keyboard_1_out_29), .in_3(keyboard_1_out_30), .in_4(keyboard_1_out_31),
    .in_5(keyboard_1_out_32), .out_9(mainboard_1_out_9), .out_10(mainboard_1_out_10),
    .out_11(mainboard_1_out_11), .out_12(mainboard_1_out_12), .out_13(mainboard_1_out_13), .Count2(out_4),
    .in_6(not_1_out), .in_7(in_1), .Count1(out_3), .rest(in_2));
  Button I (.out(I_out));
  Button O (.out(O_out));
  Button U (.out(U_out));
  Button J (.out(J_out));
  Button K (.out(K_out));
  Button M (.out(M_out));
  Button N (.out(N_out));
  Button P (.out(P_out));
  LED Q_2 (.in(output_1_q));
  Button L (.out(L_out));
  Output output_1 (
    .in_1(mainboard_1_out_9), .in_2(mainboard_1_out_10), .in_3(mainboard_1_out_11),
    .in_4(mainboard_1_out_12), .in_5(mainboard_1_out_13), .Q(output_1_q), .A(output_1_a), .Z(output_1_z),
    .W(output_1_w), .S(output_1_s), .X(output_1_x), .E(output_1_e), .D(output_1_d), .C(output_1_c),
    .R(output_1_r), .F(output_1_f), .V(output_1_v), .T(output_1_t), .G(output_1_g), .B(output_1_b),
    .Y(output_1_y), .H(output_1_h), .N(output_1_n), .U(output_1_u), .J(output_1_j), .M(output_1_m),
    .I(output_1_i), .K(output_1_k), .O(output_1_o), .L(output_1_l), .P(output_1_p));
  LED E_2 (.in(output_1_e));
  LED W_2 (.in(output_1_w));
  LED A_2 (.in(output_1_a));
  LED S_2 (.in(output_1_s));
  LED D_2 (.in(output_1_d));
  LED Z_2 (.in(output_1_z));
  LED C_2 (.in(output_1_c));
  LED X_2 (.in(output_1_x));
  LED Y_2 (.in(output_1_y));
  LED R_2 (.in(output_1_r));
  LED T_2 (.in(output_1_t));
  LED F_2 (.in(output_1_f));
  LED G_2 (.in(output_1_g));
  LED H_2 (.in(output_1_h));
  LED V_2 (.in(output_1_v));
  LED B_2 (.in(output_1_b));
  LED I_2 (.in(output_1_i));
  LED U_2 (.in(output_1_u));
  LED O_2 (.in(output_1_o));
  LED K_2 (.in(output_1_k));
  LED J_2 (.in(output_1_j));
  LED M_2 (.in(output_1_m));
  LED N_2 (.in(output_1_n));
  LED P_2 (.in(output_1_p));
  LED L_2 (.in(output_1_l));
endmodule

module Turntable1 (
  input  E,
  input  D,
  input  C,
  input  B,
  input  A,
  output E_2,
  output D_2,
  output C_2,
  output B_2,
  output A_2
);

  wire and_1_out, and_2_out, and_3_out, and_4_out, and_5_out, and_6_out, and_7_out, and_8_out, and_9_out,
       and_10_out, and_11_out, and_12_out, and_13_out, and_14_out, and_15_out, and_16_out, and_17_out,
       and_18_out, and_19_out, and_20_out, and_21_out, and_22_out, and_23_out, and_24_out, and_25_out,
       and_26_out, and_27_out, and_28_out, and_29_out, not_1_out, not_2_out, not_3_out, not_4_out, not_5_out;

  not not_1 (not_1_out, A);
  not not_2 (not_2_out, B);
  not not_3 (not_3_out, C);
  not not_4 (not_4_out, D);
  not not_5 (not_5_out, E);
  and and_1 (and_1_out, not_3_out, D, E);
  and and_2 (and_2_out, B, not_3_out, E);
  and and_3 (and_3_out, B, C, D, not_5_out);
  and and_4 (and_4_out, A, not_2_out, not_3_out, not_5_out);
  and and_5 (and_5_out, A, C, E);
  and and_6 (and_6_out, not_1_out, not_2_out, D, not_5_out);
  and and_7 (and_7_out, not_1_out, C, not_4_out, E);
  and and_8 (and_8_out, not_1_out, B, not_3_out, not_4_out, not_5_out);
  and and_9 (and_9_out, B, not_3_out, D, E);
  and and_10 (and_10_out, A, not_2_out, not_3_out, not_4_out, E);
  and and_11 (and_11_out, A, C, not_5_out);
  and and_12 (and_12_out, A, C, D);
  and and_13 (and_13_out, not_1_out, not_2_out, not_5_out);
  and and_14 (and_14_out, not_1_out, not_2_out, D);
  and and_15 (and_15_out, not_1_out, not_3_out, not_4_out);
  and and_16 (and_16_out, not_2_out, not_3_out, not_4_out, not_5_out);
  and and_17 (and_17_out, A, C, D, not_5_out);
  and and_18 (and_18_out, A, B, E);
  and and_19 (and_19_out, not_1_out, not_2_out, not_3_out, D);
  and and_20 (and_20_out, B, C, not_5_out);
  and and_21 (and_21_out, A, C, D, not_5_out);
  and and_22 (and_22_out, A, B);
  and and_23 (and_23_out, not_1_out, not_2_out, C, not_4_out);
  and and_24 (and_24_out, not_2_out, not_3_out, E);
  and and_25 (and_25_out, not_1_out, not_3_out, not_4_out);
  and and_26 (and_26_out, not_1_out, not_3_out, E);
  and and_27 (and_27_out, A, C, not_5_out);
  and and_28 (and_28_out, not_1_out, B, not_5_out);
  and and_29 (and_29_out, A, not_2_out, not_4_out, E);
  or or_1 (A_2, and_1_out, and_2_out, and_3_out, and_4_out, and_5_out);
  or or_2 (B_2, and_6_out, and_7_out, and_8_out, and_9_out, and_10_out, and_11_out, and_12_out);
  or or_3 (C_2, and_13_out, and_14_out, and_15_out, and_16_out, and_17_out, and_18_out);
  or or_4 (D_2, and_19_out, and_20_out, and_21_out, and_22_out, and_23_out, and_24_out);
  or or_5 (E_2, and_25_out, and_26_out, and_27_out, and_28_out, and_29_out);
endmodule

module Return1 (
  input  E,
  input  D,
  input  C,
  input  B,
  input  A,
  output E_2,
  output D_2,
  output C_2,
  output B_2,
  output A_2
);

  wire and_1_out, and_2_out, and_3_out, and_4_out, and_5_out, and_6_out, and_7_out, and_8_out, and_9_out,
       and_10_out, and_11_out, and_12_out, and_13_out, and_14_out, and_15_out, and_16_out, and_17_out,
       and_18_out, and_19_out, and_20_out, and_21_out, and_22_out, and_23_out, and_24_out, and_25_out,
       and_26_out, and_27_out, and_28_out, and_29_out, and_30_out, and_31_out, not_1_out, not_2_out,
       not_3_out, not_4_out, not_5_out;

  not not_1 (not_1_out, A);
  not not_2 (not_2_out, B);
  not not_3 (not_3_out, C);
  not not_4 (not_4_out, D);
  not not_5 (not_5_out, E);
  and and_1 (and_1_out, not_2_out, not_3_out, D, not_5_out);
  and and_2 (and_2_out, not_1_out, B, not_3_out, E);
  and and_3 (and_3_out, B, D, E);
  and and_4 (and_4_out, A, not_2_out, not_3_out, not_4_out);
  and and_5 (and_5_out, A, not_5_out);
  and and_6 (and_6_out, not_1_out, not_2_out, not_3_out);
  and and_7 (and_7_out, not_1_out, not_3_out, not_4_out, not_5_out);
  and and_8 (and_8_out, B, C, not_4_out, E);
  and and_9 (and_9_out, A, C, not_4_out, E);
  and and_10 (and_10_out, A, C, D, not_5_out);
  and and_11 (and_11_out, A, B, E);
  and and_12 (and_12_out, A, not_3_out, D, E);
  and and_13 (and_13_out, not_1_out, not_4_out, not_5_out);
  and and_14 (and_14_out, not_2_out, not_3_out, D, E);
  and and_15 (and_15_out, not_1_out, not_2_out, C, not_5_out);
  and and_16 (and_16_out, not_1_out, B, not_3_out, not_4_out);
  and and_17 (and_17_out, B, not_3_out, not_5_out);
  and and_18 (and_18_out, B, C, D, E);
  and and_19 (and_19_out, A, not_2_out, not_3_out, E);
  and and_20 (and_20_out, not_1_out, not_2_out, not_3_out, not_4_out);
  and and_21 (and_21_out, B, C, D);
  and and_22 (and_22_out, A, D, E);
  and and_23 (and_23_out, A, B);
  and and_24 (and_24_out, not_1_out, C, not_4_out, not_5_out);
  and and_25 (and_25_out, A, not_3_out, not_5_out);
  and and_26 (and_26_out, not_1_out, not_2_out, not_4_out, not_5_out);
  and and_27 (and_27_out, not_2_out, C, D, E);
  and and_28 (and_28_out, B, not_3_out, D);
  and and_29 (and_29_out, A, not_4_out, E);
  and and_30 (and_30_out, A, D, not_5_out);
  and and_31 (and_31_out, B, not_3_out, not_5_out);
  or or_1 (A_2, and_1_out, and_2_out, and_3_out, and_4_out, and_5_out);
  or or_2 (B_2, and_6_out, and_7_out, and_8_out, and_9_out, and_10_out, and_11_out, and_12_out);
  or or_3 (C_2, and_13_out, and_14_out, and_15_out, and_16_out, and_17_out, and_18_out, and_19_out);
  or or_4 (D_2, and_20_out, and_21_out, and_22_out, and_23_out, and_24_out, and_25_out);
  or or_5 (E_2, and_26_out, and_27_out, and_28_out, and_29_out, and_30_out, and_31_out);
endmodule

module Turntable2 (
  input  E,
  input  D,
  input  C,
  input  B,
  input  A,
  output E_2,
  output D_2,
  output C_2,
  output B_2,
  output A_2
);

  wire and_1_out, and_2_out, and_3_out, and_4_out, and_5_out, and_6_out, and_7_out, and_8_out, and_9_out,
       and_10_out, and_11_out, and_12_out, and_13_out, and_14_out, and_15_out, and_16_out, and_17_out,
       and_18_out, and_19_out, and_20_out, and_21_out, and_22_out, and_23_out, and_24_out, and_25_out,
       and_26_out, and_27_out, and_28_out, and_29_out, not_1_out, not_2_out, not_3_out, not_4_out, not_5_out;

  not not_1 (not_1_out, A);
  not not_2 (not_2_out, B);
  not not_3 (not_3_out, C);
  not not_4 (not_4_out, D);
  not not_5 (not_5_out, E);
  and and_1 (and_1_out, not_1_out, not_2_out, not_3_out, not_4_out, not_5_out);
  and and_2 (and_2_out, not_1_out, C, D, E);
  and and_3 (and_3_out, B, D, E);
  and and_4 (and_4_out, B, C, E);
  and and_5 (and_5_out, A, not_2_out, not_3_out, E);
  and and_6 (and_6_out, A, C, not_5_out);
  and and_7 (and_7_out, A, B, not_5_out);
  and and_8 (and_8_out, not_3_out, D, not_5_out);
  and and_9 (and_9_out, not_2_out, C, not_4_out, E);
  and and_10 (and_10_out, B, not_3_out, not_4_out, E);
  and and_11 (and_11_out, A, C, not_4_out);
  and and_12 (and_12_out, A, D, E);
  and and_13 (and_13_out, not_1_out, C, D);
  and and_14 (and_14_out, B, D, E);
  and and_15 (and_15_out, B, C);
  and and_16 (and_16_out, A, not_2_out, not_3_out, not_5_out);
  and and_17 (and_17_out, A, C, not_4_out, E);
  and and_18 (and_18_out, A, B, E);
  and and_19 (and_19_out, not_2_out, not_3_out, D, not_5_out);
  and and_20 (and_20_out, not_3_out, not_4_out, not_5_out);
  and and_21 (and_21_out, not_1_out, not_2_out, D, E);
  and and_22 (and_22_out, B, C, D, not_5_out);
  and and_23 (and_23_out, A, not_3_out, not_5_out);
  and and_24 (and_24_out, C, not_4_out, E);
  and and_25 (and_25_out, not_1_out, B, not_4_out, E);
  and and_26 (and_26_out, not_1_out, C, not_4_out, not_5_out);
  and and_27 (and_27_out, B, not_4_out);
  and and_28 (and_28_out, B, C);
  and and_29 (and_29_out, A, D);
  or or_1 (A_2, and_1_out, and_2_out, and_3_out, and_4_out, and_5_out, and_6_out, and_7_out);
  or or_2 (B_2, and_8_out, and_9_out, and_10_out, and_11_out, and_12_out);
  or or_3 (C_2, and_13_out, and_14_out, and_15_out, and_16_out, and_17_out, and_18_out, and_19_out);
  or or_4 (D_2, and_20_out, and_21_out, and_22_out, and_23_out, and_24_out, and_25_out);
  or or_5 (E_2, and_26_out, and_27_out, and_28_out, and_29_out);
endmodule

module Return2 (
  input  E,
  input  D,
  input  C,
  input  B,
  input  A,
  output E_2,
  output D_2,
  output C_2,
  output B_2,
  output A_2
);

  wire and_1_out, and_2_out, and_3_out, and_4_out, and_5_out, and_6_out, and_7_out, and_8_out, and_9_out,
       and_10_out, and_11_out, and_12_out, and_13_out, and_14_out, and_15_out, and_16_out, and_17_out,
       and_18_out, and_19_out, and_20_out, and_21_out, and_22_out, and_23_out, and_24_out, and_25_out,
       and_26_out, and_27_out, and_28_out, and_29_out, not_1_out, not_2_out, not_3_out, not_4_out, not_5_out;

  not not_1 (not_1_out, A);
  not not_2 (not_2_out, B);
  not not_3 (not_3_out, C);
  not not_4 (not_4_out, D);
  not not_5 (not_5_out, E);
  and and_1 (and_1_out, not_1_out, C, D, not_5_out);
  and and_2 (and_2_out, B, not_4_out, E);
  and and_3 (and_3_out, A, not_3_out, not_4_out);
  and and_4 (and_4_out, A, not_3_out, E);
  and and_5 (and_5_out, B, C, D);
  and and_6 (and_6_out, not_1_out, B, not_3_out, not_4_out, not_5_out);
  and and_7 (and_7_out, not_3_out, D, E);
  and and_8 (and_8_out, C, not_4_out, E);
  and and_9 (and_9_out, A, C, not_4_out);
  and and_10 (and_10_out, not_2_out, C, E);
  and and_11 (and_11_out, not_1_out, not_2_out, C, not_4_out);
  and and_12 (and_12_out, not_2_out, C, E);
  and and_13 (and_13_out, not_1_out, not_3_out, not_4_out, E);
  and and_14 (and_14_out, B, D, not_5_out);
  and and_15 (and_15_out, not_2_out, not_4_out, E);
  and and_16 (and_16_out, A, C, D);
  and and_17 (and_17_out, A, B, not_5_out);
  and and_18 (and_18_out, not_1_out, not_2_out, not_3_out, D, not_5_out);
  and and_19 (and_19_out, C, not_4_out, not_5_out);
  and and_20 (and_20_out, not_1_out, C, D, E);
  and and_21 (and_21_out, A, not_4_out, E);
  and and_22 (and_22_out, A, C, not_5_out);
  and and_23 (and_23_out, not_1_out, B, not_3_out, not_4_out);
  and and_24 (and_24_out, B, not_4_out, E);
  and and_25 (and_25_out, B, D, not_5_out);
  and and_26 (and_26_out, A, C);
  and and_27 (and_27_out, not_1_out, not_2_out, not_3_out, not_5_out);
  and and_28 (and_28_out, B, not_3_out, D);
  and and_29 (and_29_out, not_2_out, not_3_out, not_4_out, not_5_out);
  or or_1 (A_2, and_1_out, and_2_out, and_3_out, and_4_out, and_5_out);
  or or_2 (B_2, and_6_out, and_7_out, and_8_out, and_9_out, and_10_out);
  or or_3 (C_2, and_11_out, and_12_out, and_13_out, and_14_out, and_15_out, and_16_out, and_17_out);
  or or_4 (D_2, and_18_out, and_19_out, and_20_out, and_21_out, and_22_out, and_23_out);
  or or_5 (E_2, and_24_out, and_25_out, and_26_out, and_27_out, and_28_out, and_29_out);
endmodule

module Reflex (
  input  E,
  input  D,
  input  C,
  input  B,
  input  A,
  output E_2,
  output D_2,
  output C_2,
  output B_2,
  output A_2
);

  wire and_1_out, and_2_out, and_3_out, and_4_out, and_5_out, and_6_out, and_7_out, and_8_out, and_9_out,
       and_10_out, and_11_out, and_12_out, and_13_out, and_14_out, and_15_out, and_16_out, and_17_out,
       and_18_out, and_19_out, and_20_out, and_21_out, and_22_out, and_23_out, and_24_out, and_25_out,
       and_26_out, and_27_out, and_28_out, and_29_out, and_30_out, and_31_out, and_32_out, and_33_out,
       and_34_out, not_1_out, not_2_out, not_3_out, not_4_out, not_5_out;

  not not_1 (not_1_out, A);
  not not_2 (not_2_out, B);
  not not_3 (not_3_out, C);
  not not_4 (not_4_out, D);
  not not_5 (not_5_out, E);
  and and_1 (and_1_out, not_1_out, B, not_3_out, E);
  and and_2 (and_2_out, B, C, D);
  and and_3 (and_3_out, A, not_2_out, not_3_out, E);
  and and_4 (and_4_out, A, not_3_out, D);
  and and_5 (and_5_out, A, C, not_4_out, not_5_out);
  and and_6 (and_6_out, A, D, E);
  and and_7 (and_7_out, A, B, not_5_out);
  and and_8 (and_8_out, not_1_out, not_2_out, D, not_5_out);
  and and_9 (and_9_out, B, not_3_out, D, E);
  and and_10 (and_10_out, A, not_2_out, not_3_out, not_4_out, not_5_out);
  and and_11 (and_11_out, A, B, E);
  and and_12 (and_12_out, not_1_out, not_2_out, C, not_4_out);
  and and_13 (and_13_out, A, C, D);
  and and_14 (and_14_out, A, C, E);
  and and_15 (and_15_out, B, not_3_out, not_5_out);
  and and_16 (and_16_out, B, C, E);
  and and_17 (and_17_out, not_1_out, not_3_out, not_4_out, E);
  and and_18 (and_18_out, not_1_out, not_2_out, D, not_5_out);
  and and_19 (and_19_out, not_2_out, C, D, not_5_out);
  and and_20 (and_20_out, A, not_2_out, not_3_out, not_4_out);
  and and_21 (and_21_out, B, C, not_4_out);
  and and_22 (and_22_out, B, C, E);
  and and_23 (and_23_out, A, not_3_out, D);
  and and_24 (and_24_out, A, D, not_5_out);
  and and_25 (and_25_out, A, B);
  and and_26 (and_26_out, not_1_out, not_2_out, not_4_out, E);
  and and_27 (and_27_out, not_2_out, not_3_out, not_4_out, not_5_out);
  and and_28 (and_28_out, not_1_out, not_2_out, not_3_out, not_4_out);
  and and_29 (and_29_out, not_1_out, not_2_out, C, D);
  and and_30 (and_30_out, B, not_3_out, D);
  and and_31 (and_31_out, A, D, not_5_out);
  and and_32 (and_32_out, A, C, not_4_out);
  and and_33 (and_33_out, A, B);
  and and_34 (and_34_out, B, not_3_out, E);
  or or_1 (A_2, and_1_out, and_2_out, and_3_out, and_4_out, and_5_out, and_6_out, and_7_out);
  or or_2 (B_2, and_8_out, and_9_out, and_10_out, and_11_out, and_12_out, and_13_out, and_14_out);
  or or_3 (C_2, and_15_out, and_16_out, and_17_out, and_18_out, and_19_out, and_20_out);
  or or_4 (D_2, and_21_out, and_22_out, and_23_out, and_24_out, and_25_out, and_26_out, and_27_out);
  or or_5 (E_2, and_28_out, and_29_out, and_30_out, and_31_out, and_32_out, and_33_out, and_34_out);
endmodule

module test (
  input  in_1,
  input  [4:0] in_2,
  input  in_3,
  input  in_4,
  output [4:0] out_5
);

  wire and_1_out, clock_1_out, or_1_out;
  wire [4:0] counter_1_q;

  Clock clock_1 (.out(clock_1_out));
  Counter #(.width(5), .max('h1f)) counter_1 (
    .load(in_1), .D(in_2), .count(in_3), .Q(counter_1_q), .clk(clock_1_out), .clr(or_1_out));  // open: carry
  or or_1 (or_1_out, in_4, and_1_out);
  and and_1 (and_1_out, counter_1_q[4], counter_1_q[3], counter_1_q[1]);
  Return1 return1_1 (
    .E(counter_1_q[0]), .D(counter_1_q[1]), .C(counter_1_q[2]), .B(counter_1_q[3]), .A(counter_1_q[4]),
    .E_2(out_5[0]), .D_2(out_5[1]), .C_2(out_5[2]), .B_2(out_5[3]), .A_2(out_5[4]));
endmodule

module Keyboard (
  input  Q,
  input  W,
  input  E,
  input  R,
  input  T,
  input  Y,
  input  U,
  input  I,
  input  O,
  input  P,
  input  A,
  input  S,
  input  D,
  input  F,
  input  G,
  input  H,
  input  J,
  input  K,
  input  L,
  input  Z,
  input  X,
  input  C,
  input  V,
  input  B,
  input  N,
  input  M,
  output out_27,
  output out_28,
  output out_29,
  output out_30,
  output out_31,
  output out_32
);

  // Priority_Encoder #(.select(5)) priority_encoder_1: pin names not known; wires that end beside it: out_27, A, B, C, D, E, F, G, H, I, J, K, L, M, N, O, P, {out_28, out_29, out_30, out_31, out_32}, Q, R, S, T, U, V, W, X, Y, Z
endmodule

module Output (
  input  in_1,
  input  in_2,
  input  in_3,
  input  in_4,
  input  in_5,
  output Q,
  output W,
  output E,
  output R,
  output T,
  output Y,
  output U,
  output I,
  output O,
  output P,
  output A,
  output S,
  output D,
  output F,
  output G,
  output H,
  output J,
  output K,
  output L,
  output Z,
  output X,
  output C,
  output V,
  output B,
  output N,
  output M
);

  Decoder #(.select(5)) decoder_1 (
    .out0(A), .out1(B), .out2(C), .out3(D), .out4(E), .out5(F), .out6(G), .out7(H), .out8(I), .out9(J),
    .out10(K), .out11(L), .out12(M), .out13(N), .out14(O), .out15(P), .out16(Q), .out17(R), .out18(S),
    .out19(T), .out20(U), .out21(V), .out22(W), .out23(X), .out24(Y), .out25(Z),
    .sel({in_5, in_4, in_3, in_2, in_1}));  // open: out26, out27, out28, out29, out30, out31, en
endmodule

module MainBoard (
  input  in_1,
  input  in_2,
  input  in_3,
  input  in_4,
  input  in_5,
  input  in_6,
  input  [4:0] in_7,
  input  rest,
  output out_9,
  output out_10,
  output out_11,
  output out_12,
  output out_13,
  output [4:0] Count2,
  output [4:0] Count1
);

  wire adder_2_cout, adder_4_cout, adder_6_cout, adder_8_cout, and_1_out, and_2_out, and_3_out, and_4_out,
       and_5_out, and_6_out, and_7_out, and_8_out, and_9_out, and_10_out, and_11_out, and_12_out, and_13_out,
       and_14_out, and_15_out, and_16_out, not_1_out, not_2_out, or_1_out, or_2_out, or_3_out, or_4_out,
       or_5_out, or_6_out, or_7_out, or_8_out, or_9_out, or_10_out, or_11_out, or_12_out, or_13_out,
       or_14_out, or_15_out, or_16_out, subtractor_1_bout, subtractor_3_bout, subtractor_5_bout,
       subtractor_7_bout, xor_1_out, xor_2_out;
  wire [4:0] adder_1_out, adder_2_out, adder_3_out, adder_4_out, adder_5_out, adder_6_out, adder_7_out,
       adder_8_out, adder_9_out, multiplexer_1_out, multiplexer_2_out, multiplexer_3_out, multiplexer_4_out,
       multiplexer_5_out, multiplexer_6_out, multiplexer_7_out, multiplexer_8_out, Reflex_e_2, register_2_q,
       Return1_e_2, Return2_e_2, subtractor_1_out, subtractor_2_out, subtractor_3_out, subtractor_4_out,
       subtractor_5_out, subtractor_6_out, subtractor_7_out, turntable1_1_e_2, turntable2_1_e_2;

  not not_1 (not_1_out, in_6);
  Register #(.width(5)) register_1 (.D(adder_1_out), .Q(Count1), .clk(in_6), .clr(or_4_out));  // open: en
  Adder #(.width(5)) adder_1 (.a(in_7), .b(Count1), .out(adder_1_out));  // open: cin, cout
  Register #(.width(5)) register_2 (.D(Count1), .en(not_2_out), .Q(register_2_q), .clk(not_1_out), .clr(rest));
  not not_2 (not_2_out, or_4_out);
  Adder #(.width(5)) adder_2 (
    .a({in_1, in_2, in_3, in_4, in_5}), .b(register_2_q), .out(adder_2_out), .cout(adder_2_cout));  // open: cin
  or or_1 (or_1_out, Count1[1], Count1[2]);
  and and_1 (and_1_out, Count1[3], Count1[4]);
  or or_2 (or_2_out, adder_2_out[1], adder_2_out[2]);
  and and_2 (and_2_out, adder_2_out[3], adder_2_out[4]);
  and and_3 (and_3_out, or_1_out, and_1_out);
  and and_4 (and_4_out, or_2_out, and_2_out);
  or or_3 (or_3_out, and_4_out, adder_2_cout);
  or or_4 (or_4_out, and_3_out, rest);
  Multiplexer #(.width(5)) multiplexer_1 (
    .in0({5{1'b0}}), .in1(5'b00110), .out(multiplexer_1_out), .sel(or_3_out));  // open: en
  Counter #(.width(5), .max('h1f)) counter_1 (
    .count(1'b1), .Q(Count2), .clk(or_4_out), .clr(or_6_out));  // open: load, D, carry
  Turntable1 turntable1_1 (
    .E(adder_3_out[0]), .D(adder_3_out[1]), .C(adder_3_out[2]), .B(adder_3_out[3]), .A(adder_3_out[4]),
    .E_2(turntable1_1_e_2[0]), .D_2(turntable1_1_e_2[1]), .C_2(turntable1_1_e_2[2]),
    .B_2(turntable1_1_e_2[3]), .A_2(turntable1_1_e_2[4]));
  Adder #(.width(5)) adder_3 (.a(multiplexer_1_out), .b(adder_2_out), .out(adder_3_out));  // open: cin, cout
  Subtractor #(.width(5)) subtractor_1 (
    .a(Count2), .b(register_2_q), .out(subtractor_1_out), .bout(subtractor_1_bout));  // open: bin
  or or_5 (or_5_out, Count2[1], Count2[2]);
  and and_5 (and_5_out, Count2[3], Count2[4]);
  Adder #(.width(5)) adder_4 (
    .a(turntable1_1_e_2), .b(subtractor_1_out), .out(adder_4_out), .cout(adder_4_cout));  // open: cin
  xor xor_1 (xor_1_out, adder_4_cout, subtractor_1_bout);
  and and_6 (and_6_out, or_5_out, and_5_out);
  or or_6 (or_6_out, and_6_out, rest);
  or or_7 (or_7_out, adder_4_out[1], adder_4_out[2]);
  and and_7 (and_7_out, adder_4_out[3], adder_4_out[4]);
  and and_8 (and_8_out, or_7_out, and_7_out);
  or or_8 (or_8_out, and_8_out, xor_1_out);
  Multiplexer #(.width(5)) multiplexer_2 (
    .in0({5{1'b0}}), .in1(5'b00110), .out(multiplexer_2_out), .sel(or_8_out));  // open: en
  Adder #(.width(5)) adder_5 (.a(multiplexer_2_out), .b(adder_4_out), .out(adder_5_out));  // open: cin, cout
  Subtractor #(.width(5)) subtractor_2 (
    .a(adder_4_out), .b(multiplexer_2_out), .out(subtractor_2_out));  // open: bin, bout
  Multiplexer #(.width(5)) multiplexer_3 (
    .in0(adder_5_out), .in1(subtractor_2_out), .out(multiplexer_3_out), .sel(subtractor_1_bout));  // open: en
  Turntable2 turntable2_1 (
    .E(multiplexer_3_out[0]), .D(multiplexer_3_out[1]), .C(multiplexer_3_out[2]), .B(multiplexer_3_out[3]),
    .A(multiplexer_3_out[4]), .E_2(turntable2_1_e_2[0]), .D_2(turntable2_1_e_2[1]),
    .C_2(turntable2_1_e_2[2]), .B_2(turntable2_1_e_2[3]), .A_2(turntable2_1_e_2[4]));
  Subtractor #(.width(5)) subtractor_3 (
    .a(turntable2_1_e_2), .b(Count2), .out(subtractor_3_out), .bout(subtractor_3_bout));  // open: bin
  or or_9 (or_9_out, subtractor_3_out[1], subtractor_3_out[2]);
  and and_9 (and_9_out, or_9_out, and_10_out);
  and and_10 (and_10_out, subtractor_3_out[3], subtractor_3_out[4]);
  or or_10 (or_10_out, and_9_out, subtractor_3_bout);
  Multiplexer #(.width(5)) multiplexer_4 (
    .in0({5{1'b0}}), .in1(5'b00110), .out(multiplexer_4_out), .sel(or_10_out));  // open: en
  Subtractor #(.width(5)) subtractor_4 (
    .a(subtractor_3_out), .b(multiplexer_4_out), .out(subtractor_4_out));  // open: bin, bout
  Reflex Reflex (
    .E(subtractor_4_out[0]), .D(subtractor_4_out[1]), .C(subtractor_4_out[2]), .B(subtractor_4_out[3]),
    .A(subtractor_4_out[4]), .E_2(Reflex_e_2[0]), .D_2(Reflex_e_2[1]), .C_2(Reflex_e_2[2]),
    .B_2(Reflex_e_2[3]), .A_2(Reflex_e_2[4]));
  Adder #(.width(5)) adder_6 (.a(Reflex_e_2), .b(Count2), .out(adder_6_out), .cout(adder_6_cout));  // open: cin
  or or_11 (or_11_out, adder_6_out[1], adder_6_out[2]);
  and and_11 (and_11_out, adder_6_out[3], adder_6_out[4]);
  and and_12 (and_12_out, or_11_out, and_11_out);
  or or_12 (or_12_out, and_12_out, adder_6_cout);
  Multiplexer #(.width(5)) multiplexer_5 (
    .in0({5{1'b0}}), .in1(5'b00110), .out(multiplexer_5_out), .sel(or_12_out));  // open: en
  Return2 Return2 (
    .E(adder_7_out[0]), .D(adder_7_out[1]), .C(adder_7_out[2]), .B(adder_7_out[3]), .A(adder_7_out[4]),
    .E_2(Return2_e_2[0]), .D_2(Return2_e_2[1]), .C_2(Return2_e_2[2]), .B_2(Return2_e_2[3]),
    .A_2(Return2_e_2[4]));
  Adder #(.width(5)) adder_7 (.a(multiplexer_5_out), .b(adder_6_out), .out(adder_7_out));  // open: cin, cout
  Subtractor #(.width(5)) subtractor_5 (
    .a(register_2_q), .b(Count2), .out(subtractor_5_out), .bout(subtractor_5_bout));  // open: bin
  Adder #(.width(5)) adder_8 (
    .a(Return2_e_2), .b(subtractor_5_out), .out(adder_8_out), .cout(adder_8_cout));  // open: cin
  xor xor_2 (xor_2_out, adder_8_cout, subtractor_5_bout);
  or or_13 (or_13_out, adder_8_out[1], adder_8_out[2]);
  and and_13 (and_13_out, adder_8_out[3], adder_8_out[4]);
  and and_14 (and_14_out, or_13_out, and_13_out);
  or or_14 (or_14_out, and_14_out, xor_2_out);
  Multiplexer #(.width(5)) multiplexer_6 (
    .in0({5{1'b0}}), .in1(5'b00110), .out(multiplexer_6_out), .sel(or_14_out));  // open: en
  Adder #(.width(5)) adder_9 (.a(multiplexer_6_out), .b(adder_8_out), .out(adder_9_out));  // open: cin, cout
  Multiplexer #(.width(5)) multiplexer_7 (
    .in0(adder_9_out), .in1(subtractor_6_out), .out(multiplexer_7_out), .sel(subtractor_5_bout));  // open: en
  Subtractor #(.width(5)) subtractor_6 (
    .a(adder_8_out), .b(multiplexer_6_out), .out(subtractor_6_out));  // open: bin, bout
  Return1 Return1 (
    .E(multiplexer_7_out[0]), .D(multiplexer_7_out[1]), .C(multiplexer_7_out[2]), .B(multiplexer_7_out[3]),
    .A(multiplexer_7_out[4]), .E_2(Return1_e_2[0]), .D_2(Return1_e_2[1]), .C_2(Return1_e_2[2]),
    .B_2(Return1_e_2[3]), .A_2(Return1_e_2[4]));
  Subtractor #(.width(5)) subtractor_7 (
    .a(Return1_e_2), .b(register_2_q), .out(subtractor_7_out), .bout(subtractor_7_bout));  // open: bin
  or or_15 (or_15_out, subtractor_7_out[1], subtractor_7_out[2]);
  and and_15 (and_15_out, subtractor_7_out[3], subtractor_7_out[4]);
  and and_16 (and_16_out, or_15_out, and_15_out);
  or or_16 (or_16_out, and_16_out, subtractor_7_bout);
  Multiplexer #(.width(5)) multiplexer_8 (
    .in0({5{1'b0}}), .in1(5'b00110), .out(multiplexer_8_out), .sel(or_16_out));  // open: en
  Subtractor #(.width(5)) subtractor_8 (
    .a(subtractor_7_out), .b(multiplexer_8_out), .out({out_13, out_12, out_11, out_10, out_9}));  // open: bin, bout
endmodule

module test2 (
  input  in_1,
  input  in_2,
  input  in_3,
  input  in_4,
  input  in_5,
  input  in_6,
  input  [4:0] in_7,
  input  rest,
  output out_9,
  output out_10,
  output out_11,
  output out_12,
  output out_13,
  output [4:0] Count2,
  output [4:0] Count1
);

  wire adder_2_cout, adder_4_cout, adder_6_cout, adder_8_cout, and_1_out, and_2_out, and_3_out, and_4_out,
       and_5_out, and_6_out, and_7_out, and_8_out, and_9_out, and_10_out, and_11_out, and_12_out, and_13_out,
       and_14_out, and_15_out, and_16_out, not_1_out, not_2_out, or_1_out, or_2_out, or_3_out, or_4_out,
       or_5_out, or_6_out, or_7_out, or_8_out, or_9_out, or_10_out, or_11_out, or_12_out, or_13_out,
       or_14_out, or_15_out, or_16_out, subtractor_1_bout, subtractor_3_bout, subtractor_5_bout,
       subtractor_7_bout, xor_1_out, xor_2_out;
  wire [4:0] adder_1_out, adder_2_out, adder_3_out, adder_4_out, adder_5_out, adder_6_out, adder_7_out,
       adder_8_out, adder_9_out, multiplexer_1_out, multiplexer_2_out, multiplexer_3_out, multiplexer_4_out,
       multiplexer_5_out, multiplexer_6_out, multiplexer_7_out, multiplexer_8_out, Reflex_e_2, register_2_q,
       Return1_e_2, Return2_e_2, subtractor_1_out, subtractor_2_out, subtractor_3_out, subtractor_4_out,
       subtractor_5_out, subtractor_6_out, subtractor_7_out, turntable1_1_e_2, turntable2_1_e_2;

  not not_1 (not_1_out, in_6);
  Adder #(.width(5)) adder_1 (.a(in_7), .b(Count1), .out(adder_1_out));  // open: cin, cout
  Register #(.width(5)) register_1 (.D(adder_1_out), .Q(Count1), .clk(in_6), .clr(or_4_out));  // open: en
  Register #(.width(5)) register_2 (.D(Count1), .en(not_2_out), .Q(register_2_q), .clk(not_1_out), .clr(rest));
  not not_2 (not_2_out, or_4_out);
  Adder #(.width(5)) adder_2 (
    .a({in_1, in_2, in_3, in_4, in_5}), .b(register_2_q), .out(adder_2_out), .cout(adder_2_cout));  // open: cin
  or or_1 (or_1_out, Count1[1], Count1[2]);
  and and_1 (and_1_out, Count1[3], Count1[4]);
  or or_2 (or_2_out, adder_2_out[0], adder_2_out[1], adder_2_out[2]);
  and and_2 (and_2_out, adder_2_out[3], adder_2_out[4]);
  and and_3 (and_3_out, or_1_out, and_1_out);
  and and_4 (and_4_out, or_2_out, and_2_out);
  or or_3 (or_3_out, and_4_out, adder_2_cout);
  or or_4 (or_4_out, and_3_out, rest);
  Multiplexer #(.width(5)) multiplexer_1 (
    .in0({5{1'b0}}), .in1(5'b00110), .out(multiplexer_1_out), .sel(or_3_out));  // open: en
  Counter #(.width(5), .max('h1f)) counter_1 (
    .count(1'b1), .Q(Count2), .clk(or_4_out), .clr(or_6_out));  // open: load, D, carry
  Turntable1 turntable1_1 (
    .E(adder_3_out[0]), .D(adder_3_out[1]), .C(adder_3_out[2]), .B(adder_3_out[3]), .A(adder_3_out[4]),
    .E_2(turntable1_1_e_2[0]), .D_2(turntable1_1_e_2[1]), .C_2(turntable1_1_e_2[2]),
    .B_2(turntable1_1_e_2[3]), .A_2(turntable1_1_e_2[4]));
  Adder #(.width(5)) adder_3 (.a(multiplexer_1_out), .b(adder_2_out), .out(adder_3_out));  // open: cin, cout
  Subtractor #(.width(5)) subtractor_1 (
    .a(Count2), .b(register_2_q), .out(subtractor_1_out), .bout(subtractor_1_bout));  // open: bin
  or or_5 (or_5_out, Count2[1], Count2[2]);
  and and_5 (and_5_out, Count2[3], Count2[4]);
  Adder #(.width(5)) adder_4 (
    .a(turntable1_1_e_2), .b(subtractor_1_out), .out(adder_4_out), .cout(adder_4_cout));  // open: cin
  xor xor_1 (xor_1_out, adder_4_cout, subtractor_1_bout);
  and and_6 (and_6_out, or_5_out, and_5_out);
  or or_6 (or_6_out, and_6_out, rest);
  or or_7 (or_7_out, adder_4_out[0], adder_4_out[1], adder_4_out[2]);
  and and_7 (and_7_out, adder_4_out[3], adder_4_out[4]);
  and and_8 (and_8_out, or_7_out, and_7_out);
  or or_8 (or_8_out, and_8_out, xor_1_out);
  Multiplexer #(.width(5)) multiplexer_2 (
    .in0({5{1'b0}}), .in1(5'b00110), .out(multiplexer_2_out), .sel(or_8_out));  // open: en
  Adder #(.width(5)) adder_5 (.a(multiplexer_2_out), .b(adder_4_out), .out(adder_5_out));  // open: cin, cout
  Subtractor #(.width(5)) subtractor_2 (
    .a(adder_4_out), .b(multiplexer_2_out), .out(subtractor_2_out));  // open: bin, bout
  Multiplexer #(.width(5)) multiplexer_3 (
    .in0(adder_5_out), .in1(subtractor_2_out), .out(multiplexer_3_out), .sel(subtractor_1_bout));  // open: en
  Turntable2 turntable2_1 (
    .E(multiplexer_3_out[0]), .D(multiplexer_3_out[1]), .C(multiplexer_3_out[2]), .B(multiplexer_3_out[3]),
    .A(multiplexer_3_out[4]), .E_2(turntable2_1_e_2[0]), .D_2(turntable2_1_e_2[1]),
    .C_2(turntable2_1_e_2[2]), .B_2(turntable2_1_e_2[3]), .A_2(turntable2_1_e_2[4]));
  Subtractor #(.width(5)) subtractor_3 (
    .a(turntable2_1_e_2), .b(Count2), .out(subtractor_3_out), .bout(subtractor_3_bout));  // open: bin
  or or_9 (or_9_out, subtractor_3_out[0], subtractor_3_out[1], subtractor_3_out[2]);
  and and_9 (and_9_out, or_9_out, and_10_out);
  and and_10 (and_10_out, subtractor_3_out[3], subtractor_3_out[4]);
  or or_10 (or_10_out, and_9_out, subtractor_3_bout);
  Multiplexer #(.width(5)) multiplexer_4 (
    .in0({5{1'b0}}), .in1(5'b00110), .out(multiplexer_4_out), .sel(or_10_out));  // open: en
  Subtractor #(.width(5)) subtractor_4 (
    .a(subtractor_3_out), .b(multiplexer_4_out), .out(subtractor_4_out));  // open: bin, bout
  Reflex Reflex (
    .E(subtractor_4_out[0]), .D(subtractor_4_out[1]), .C(subtractor_4_out[2]), .B(subtractor_4_out[3]),
    .A(subtractor_4_out[4]), .E_2(Reflex_e_2[0]), .D_2(Reflex_e_2[1]), .C_2(Reflex_e_2[2]),
    .B_2(Reflex_e_2[3]), .A_2(Reflex_e_2[4]));
  Adder #(.width(5)) adder_6 (.a(Reflex_e_2), .b(Count2), .out(adder_6_out), .cout(adder_6_cout));  // open: cin
  or or_11 (or_11_out, adder_6_out[0], adder_6_out[1], adder_6_out[2]);
  and and_11 (and_11_out, adder_6_out[3], adder_6_out[4]);
  and and_12 (and_12_out, or_11_out, and_11_out);
  or or_12 (or_12_out, and_12_out, adder_6_cout);
  Multiplexer #(.width(5)) multiplexer_5 (
    .in0({5{1'b0}}), .in1(5'b00110), .out(multiplexer_5_out), .sel(or_12_out));  // open: en
  Return2 Return2 (
    .E(adder_7_out[0]), .D(adder_7_out[1]), .C(adder_7_out[2]), .B(adder_7_out[3]), .A(adder_7_out[4]),
    .E_2(Return2_e_2[0]), .D_2(Return2_e_2[1]), .C_2(Return2_e_2[2]), .B_2(Return2_e_2[3]),
    .A_2(Return2_e_2[4]));
  Adder #(.width(5)) adder_7 (.a(multiplexer_5_out), .b(adder_6_out), .out(adder_7_out));  // open: cin, cout
  Subtractor #(.width(5)) subtractor_5 (
    .a(register_2_q), .b(Count2), .out(subtractor_5_out), .bout(subtractor_5_bout));  // open: bin
  Adder #(.width(5)) adder_8 (
    .a(Return2_e_2), .b(subtractor_5_out), .out(adder_8_out), .cout(adder_8_cout));  // open: cin
  xor xor_2 (xor_2_out, adder_8_cout, subtractor_5_bout);
  or or_13 (or_13_out, adder_8_out[0], adder_8_out[1], adder_8_out[2]);
  and and_13 (and_13_out, adder_8_out[3], adder_8_out[4]);
  and and_14 (and_14_out, or_13_out, and_13_out);
  or or_14 (or_14_out, and_14_out, xor_2_out);
  Multiplexer #(.width(5)) multiplexer_6 (
    .in0({5{1'b0}}), .in1(5'b00110), .out(multiplexer_6_out), .sel(or_14_out));  // open: en
  Adder #(.width(5)) adder_9 (.a(multiplexer_6_out), .b(adder_8_out), .out(adder_9_out));  // open: cin, cout
  Multiplexer #(.width(5)) multiplexer_7 (
    .in0(adder_9_out), .in1(subtractor_6_out), .out(multiplexer_7_out), .sel(subtractor_5_bout));  // open: en
  Subtractor #(.width(5)) subtractor_6 (
    .a(adder_8_out), .b(multiplexer_6_out), .out(subtractor_6_out));  // open: bin, bout
  Return1 Return1 (
    .E(multiplexer_7_out[0]), .D(multiplexer_7_out[1]), .C(multiplexer_7_out[2]), .B(multiplexer_7_out[3]),
    .A(multiplexer_7_out[4]), .E_2(Return1_e_2[0]), .D_2(Return1_e_2[1]), .C_2(Return1_e_2[2]),
    .B_2(Return1_e_2[3]), .A_2(Return1_e_2[4]));
  Subtractor #(.width(5)) subtractor_7 (
    .a(Return1_e_2), .b(register_2_q), .out(subtractor_7_out), .bout(subtractor_7_bout));  // open: bin
  or or_15 (or_15_out, subtractor_7_out[0], subtractor_7_out[1], subtractor_7_out[2]);
  and and_15 (and_15_out, subtractor_7_out[3], subtractor_7_out[4]);
  and and_16 (and_16_out, or_15_out, and_15_out);
  or or_16 (or_16_out, and_16_out, subtractor_7_bout);
  Multiplexer #(.width(5)) multiplexer_8 (
    .in0({5{1'b0}}), .in1(5'b00110), .out(multiplexer_8_out), .sel(or_16_out));  // open: en
  Subtractor #(.width(5)) subtractor_8 (
    .a(subtractor_7_out), .b(multiplexer_8_out), .out({out_13, out_12, out_11, out_10, out_9}));  // open: bin, bout
endmodule

module test3 (
);

  wire A_out, B_out, C_out, D_out, E_out, F_out, G_out, H_out, I_out, J_out, K_out, keyboard_1_out_28,
       keyboard_1_out_29, keyboard_1_out_30, keyboard_1_out_31, keyboard_1_out_32, L_out, M_out, N_out,
       O_out, output_1_a, output_1_b, output_1_c, output_1_d, output_1_e, output_1_f, output_1_g, output_1_h,
       output_1_i, output_1_j, output_1_k, output_1_l, output_1_m, output_1_n, output_1_o, output_1_p,
       output_1_q, output_1_r, output_1_s, output_1_t, output_1_u, output_1_v, output_1_w, output_1_x,
       output_1_y, output_1_z, P_out, Q_out, R_out, reflex_1_a_2, reflex_1_b_2, reflex_1_c_2, reflex_1_d_2,
       reflex_1_e_2, return1_1_a_2, return1_1_b_2, return1_1_c_2, return1_1_d_2, return1_1_e_2,
       return2_1_a_2, return2_1_b_2, return2_1_c_2, return2_1_d_2, return2_1_e_2, S_out, T_out,
       turntable1_1_a_2, turntable1_1_b_2, turntable1_1_c_2, turntable1_1_d_2, turntable1_1_e_2,
       turntable2_1_a_2, turntable2_1_b_2, turntable2_1_c_2, turntable2_1_d_2, turntable2_1_e_2, U_out,
       V_out, W_out, X_out, Y_out, Z_out;

  Button Q (.out(Q_out));
  Keyboard keyboard_1 (
    .Q(Q_out), .A(A_out), .Z(Z_out), .W(W_out), .S(S_out), .X(X_out), .E(E_out), .D(D_out), .C(C_out),
    .R(R_out), .F(F_out), .V(V_out), .T(T_out), .G(G_out), .B(B_out), .Y(Y_out), .H(H_out), .N(N_out),
    .U(U_out), .J(J_out), .M(M_out), .I(I_out), .K(K_out), .O(O_out), .L(L_out), .P(P_out),
    .out_28(keyboard_1_out_28), .out_29(keyboard_1_out_29), .out_30(keyboard_1_out_30),
    .out_31(keyboard_1_out_31), .out_32(keyboard_1_out_32));  // open: out_27
  Button W (.out(W_out));
  Button E (.out(E_out));
  Button S (.out(S_out));
  Button A (.out(A_out));
  Button D (.out(D_out));
  Button Z (.out(Z_out));
  Button X (.out(X_out));
  Button C (.out(C_out));
  Button T (.out(T_out));
  Button Y (.out(Y_out));
  Button R (.out(R_out));
  Button G (.out(G_out));
  Button H (.out(H_out));
  Button F (.out(F_out));
  Button B (.out(B_out));
  Button V (.out(V_out));
  Button I (.out(I_out));
  Button O (.out(O_out));
  Button U (.out(U_out));
  Button J (.out(J_out));
  Button K (.out(K_out));
  Button M (.out(M_out));
  Button N (.out(N_out));
  Turntable1 turntable1_1 (
    .E(keyboard_1_out_32), .D(keyboard_1_out_31), .C(keyboard_1_out_30), .B(keyboard_1_out_29),
    .A(keyboard_1_out_28), .E_2(turntable1_1_e_2), .D_2(turntable1_1_d_2), .C_2(turntable1_1_c_2),
    .B_2(turntable1_1_b_2), .A_2(turntable1_1_a_2));
  Turntable2 turntable2_1 (
    .E(turntable1_1_e_2), .D(turntable1_1_d_2), .C(turntable1_1_c_2), .B(turntable1_1_b_2),
    .A(turntable1_1_a_2), .E_2(turntable2_1_e_2), .D_2(turntable2_1_d_2), .C_2(turntable2_1_c_2),
    .B_2(turntable2_1_b_2), .A_2(turntable2_1_a_2));
  Button P (.out(P_out));
  Button L (.out(L_out));
  Reflex reflex_1 (
    .E(turntable2_1_e_2), .D(turntable2_1_d_2), .C(turntable2_1_c_2), .B(turntable2_1_b_2),
    .A(turntable2_1_a_2), .E_2(reflex_1_e_2), .D_2(reflex_1_d_2), .C_2(reflex_1_c_2), .B_2(reflex_1_b_2),
    .A_2(reflex_1_a_2));
  Return1 return1_1 (
    .E(return2_1_e_2), .D(return2_1_d_2), .C(return2_1_c_2), .B(return2_1_b_2), .A(return2_1_a_2),
    .E_2(return1_1_e_2), .D_2(return1_1_d_2), .C_2(return1_1_c_2), .B_2(return1_1_b_2), .A_2(return1_1_a_2));
  Return2 return2_1 (
    .E(reflex_1_e_2), .D(reflex_1_d_2), .C(reflex_1_c_2), .B(reflex_1_b_2), .A(reflex_1_a_2),
    .E_2(return2_1_e_2), .D_2(return2_1_d_2), .C_2(return2_1_c_2), .B_2(return2_1_b_2), .A_2(return2_1_a_2));
  LED Q_2 (.in(output_1_q));
  LED W_2 (.in(output_1_w));
  LED S_2 (.in(output_1_s));
  LED A_2 (.in(output_1_a));
  LED X_2 (.in(output_1_x));
  LED Z_2 (.in(output_1_z));
  Output output_1 (
    .in_1(return1_1_e_2), .in_2(return1_1_d_2), .in_3(return1_1_c_2), .in_4(return1_1_b_2),
    .in_5(return1_1_a_2), .Q(output_1_q), .A(output_1_a), .Z(output_1_z), .W(output_1_w), .S(output_1_s),
    .X(output_1_x), .E(output_1_e), .D(output_1_d), .C(output_1_c), .R(output_1_r), .F(output_1_f),
    .V(output_1_v), .T(output_1_t), .G(output_1_g), .B(output_1_b), .Y(output_1_y), .H(output_1_h),
    .N(output_1_n), .U(output_1_u), .J(output_1_j), .M(output_1_m), .I(output_1_i), .K(output_1_k),
    .O(output_1_o), .L(output_1_l), .P(output_1_p));
  LED R_2 (.in(output_1_r));
  LED T_2 (.in(output_1_t));
  LED E_2 (.in(output_1_e));
  LED F_2 (.in(output_1_f));
  LED G_2 (.in(output_1_g));
  LED D_2 (.in(output_1_d));
  LED C_2 (.in(output_1_c));
  LED V_2 (.in(output_1_v));
  LED Y_2 (.in(output_1_y));
  LED I_2 (.in(output_1_i));
  LED U_2 (.in(output_1_u));
  LED H_2 (.in(output_1_h));
  LED J_2 (.in(output_1_j));
  LED M_2 (.in(output_1_m));
  LED B_2 (.in(output_1_b));
  LED N_2 (.in(output_1_n));
  LED P_2 (.in(output_1_p));
  LED O_2 (.in(output_1_o));
  LED K_2 (.in(output_1_k));
  LED L_2 (.in(output_1_l));
endmodule
