// Logisim project Enigma.circ as structural Verilog: 1 circuit, main circuit InputC
module InputC (
  input  in_1,
  input  in_2,
  input  Input,
  input  in_4,
  input  in_5,
  input  in_6,
  input  [7:0] in_7,
  output [7:0] Output
);

  wire counter_1_carry, counter_2_carry, counter_3_carry;
  wire [7:0] adder_1_out, adder_2_out, adder_4_out, adder_5_out, adder_6_out, counter_1_q, counter_2_q,
       counter_3_q, counter_4_q, rom_1_data, rom_2_data, rom_3_data, rom_4_data, subtractor_1_out,
       subtractor_2_out, subtractor_3_out;

  Counter #(.max('h19)) counter_1 (
    .Q(counter_1_q), .carry(counter_1_carry), .clk(counter_2_carry), .clr(counter_1_carry));  // open: load, D, count
  Counter #(.max('h19)) counter_2 (
    .Q(counter_2_q), .carry(counter_2_carry), .clk(counter_3_carry), .clr(counter_2_carry));  // open: load, D, count
  Counter #(.max('h19)) counter_3 (
    .Q(counter_3_q), .carry(counter_3_carry), .clk(in_1), .clr(counter_3_carry));  // open: load, D, count
  Counter #(.max('h19)) counter_4 (.Q(counter_4_q), .clk(Input));  // open: load, D, count, carry, clr
  Adder adder_1 (.a(counter_3_q), .b(counter_4_q), .out(adder_1_out));  // open: cin, cout
  ROM rom_1 (.addr(adder_1_out), .data(rom_1_data), .sel(in_2));
  Adder adder_2 (.a(counter_2_q), .b(rom_1_data), .out(adder_2_out));  // open: cin, cout
  Subtractor subtractor_1 (.a(adder_2_out), .b(in_7), .out(subtractor_1_out));  // open: bin, bout
  Adder adder_3 (.a(adder_5_out), .b(subtractor_1_out), .out(Output));  // open: cin, cout
  ROM rom_2 (.addr(subtractor_1_out), .data(rom_2_data), .sel(in_4));
  Adder adder_4 (.a(counter_1_q), .b(rom_2_data), .out(adder_4_out));  // open: cin, cout
  Subtractor subtractor_2 (.a(adder_4_out), .b(in_7), .out(subtractor_2_out));  // open: bin, bout
  Adder adder_5 (.a(adder_6_out), .b(subtractor_2_out), .out(adder_5_out));  // open: cin, cout
  ROM rom_3 (.addr(subtractor_2_out), .data(rom_3_data), .sel(in_5));
  Subtractor subtractor_3 (.a(rom_3_data), .b(in_7), .out(subtractor_3_out));  // open: bin, bout
  Adder adder_6 (.a(rom_4_data), .b(subtractor_3_out), .out(adder_6_out));  // open: cin, cout
  ROM rom_4 (.addr(subtractor_3_out), .data(rom_4_data), .sel(in_6));

  // Notes on the sheet:
  //   Count
  //   RoterRight
  //   01000001
  //   contents of rom_1 (hex, n*v repeats v):
  //   41 42 43 44 45 46 47 48 49 4a 4b 4c 4d 4e 4f 50 51 52 53 54 55 56 57 58 59 5a
  //   RoterMiddle
  //   contents of rom_2 (hex, n*v repeats v):
  //   41 42 43 44 45 46 47 48 49 4a 4b 4c 4d 4e 4f 50 51 52 53 54 55 56 57 58 59 5a
  //   RoterLeft
  //   contents of rom_3 (hex, n*v repeats v):
  //   41 42 43 44 45 46 47 48 49 4a 4b 4c 4d 4e 4f 50 51 52 53 54 55 56 57 58 59 5a
  //   Refelctor
  //   contents of rom_4 (hex, n*v repeats v):
  //   41 42 43 44 45 46 47 48 49 4a 4b 4c 4d 4e 4f 50 51 52 53 54 55 56 57 58 59 5a
endmodule
