// Logisim project enigma_logisim.circ as structural Verilog: 1 circuit, main circuit main
module main (
  input  [4:0] in_1,
  input  [4:0] in_2,
  input  [4:0] in_3,
  input  [4:0] in_4
);

  wire and_1_out, and_2_out, and_3_out, and_4_out, and_5_out, and_6_out, and_7_out, and_8_out, and_9_out,
       and_10_out, and_11_out, and_12_out, and_13_out, and_14_out, and_15_out, and_16_out, and_17_out,
       and_18_out, and_19_out, and_20_out, and_21_out, and_22_out, and_23_out, and_24_out, and_25_out,
       and_26_out, and_27_out, and_28_out, and_29_out, and_30_out, and_31_out, and_32_out, and_33_out,
       and_34_out, and_35_out, and_36_out, and_37_out, and_38_out, and_39_out, and_40_out, not_1_out,
       not_2_out, not_3_out, not_4_out, not_5_out, not_6_out, not_7_out, not_8_out, not_9_out, not_10_out,
       not_11_out, not_12_out, not_13_out, not_14_out, not_15_out, or_1_out, or_2_out, or_3_out, or_4_out,
       or_9_out, or_10_out, or_11_out, or_12_out;

  not not_1 (not_1_out, in_1[0]);
  not not_2 (not_2_out, in_1[1]);
  not not_3 (not_3_out, in_1[2]);
  not not_4 (not_4_out, in_1[3]);
  not not_5 (not_5_out, in_1[4]);
  not not_6 (not_6_out, in_2[0]);
  not not_7 (not_7_out, in_2[1]);
  not not_8 (not_8_out, in_2[2]);
  not not_9 (not_9_out, in_2[3]);
  not not_10 (not_10_out, in_2[4]);
  not not_11 (not_11_out, in_3[0]);
  not not_12 (not_12_out, in_3[1]);
  not not_13 (not_13_out, in_3[2]);
  not not_14 (not_14_out, in_3[3]);
  not not_15 (not_15_out, in_3[4]);
  and and_1 (and_1_out, not_10_out, not_7_out);
  and and_2 (and_2_out, not_9_out, not_7_out);
  and and_3 (and_3_out, not_8_out, in_2[1]);
  and and_4 (and_4_out, in_2[2], not_7_out);
  and and_5 (and_5_out, not_10_out, in_2[3], not_7_out);
  and and_6 (and_6_out, not_9_out, in_2[3], in_2[1]);
  and and_7 (and_7_out, in_2[3], not_8_out, in_2[1]);
  and and_8 (and_8_out, in_2[3], in_2[2], in_2[1]);
  and and_9 (and_9_out, in_2[4], not_9_out);
  and and_10 (and_10_out, not_15_out, not_12_out, not_11_out);
  and and_11 (and_11_out, not_14_out, not_12_out, not_11_out);
  and and_12 (and_12_out, not_15_out, in_3[1], in_3[0]);
  and and_13 (and_13_out, not_13_out, in_3[1], in_3[0]);
  and and_14 (and_14_out, in_3[4], in_3[3], in_3[0]);
  and and_15 (and_15_out, not_15_out, not_13_out, in_3[0]);
  and and_16 (and_16_out, not_14_out, not_13_out, in_3[0]);
  and and_17 (and_17_out, in_3[2], not_12_out, not_11_out);
  and and_18 (and_18_out, not_13_out, in_3[1]);
  and and_19 (and_19_out, not_14_out, in_3[2], not_12_out, in_3[0]);
  and and_20 (and_20_out, not_15_out, not_14_out, in_3[2], in_3[1]);
  and and_21 (and_21_out, in_3[3], in_3[2], not_12_out, not_11_out);
  and and_22 (and_22_out, in_3[4], in_3[2], in_3[1], not_11_out);
  and and_23 (and_23_out, not_15_out, in_3[3], not_13_out);
  and and_24 (and_24_out, not_15_out, in_3[3], in_3[2], in_3[1]);
  and and_25 (and_25_out, in_3[4], not_14_out, not_12_out);
  and and_26 (and_26_out, in_3[4], not_13_out, in_3[1]);
  and and_27 (and_27_out, in_3[4], not_13_out, in_3[2]);
  and and_28 (and_28_out, in_3[4], in_3[2], not_11_out);
  and and_29 (and_29_out, not_2_out, in_1[0]);
  and and_30 (and_30_out, not_1_out, in_1[1]);
  and and_31 (and_31_out, not_3_out, in_1[1], in_1[0]);
  and and_32 (and_32_out, in_1[2], not_2_out);
  and and_33 (and_33_out, in_1[2], not_1_out);
  and and_34 (and_34_out, not_4_out, in_1[2], in_1[1], in_1[0]);
  and and_35 (and_35_out, not_5_out, in_1[3], not_2_out);
  and and_36 (and_36_out, in_1[3], not_3_out, in_1[1]);
  and and_37 (and_37_out, in_1[3], not_1_out);
  and and_38 (and_38_out, in_1[3], in_1[2], in_1[1], in_1[0]);
  and and_39 (and_39_out, in_1[4], not_4_out);
  and and_40 (and_40_out, in_1[4], not_1_out);
  Keyboard keyboard_1 ();  // open: clk, re, clr, avail, data
  or or_1 (or_1_out, and_1_out, and_2_out);
  LED led_1 (.in(or_1_out));
  or or_2 (or_2_out, and_3_out, and_4_out);
  LED led_2 (.in(or_2_out));
  LED led_3 (.in(or_3_out));
  or or_3 (or_3_out, and_5_out, and_6_out, and_7_out);
  LED led_4 (.in(in_2[0]));
  or or_4 (or_4_out, and_8_out, and_9_out);
  LED led_5 (.in(or_4_out));
  // OR_Gate or_5 has open pins: in0=and_10_out, in1=and_11_out, in2=and_12_out, in3=and_13_out, in4=and_14_out, out=open
  // OR_Gate or_6 has open pins: in0=and_15_out, in1=and_16_out, in3=and_17_out, in4=and_18_out, out=open
  // OR_Gate or_7 has open pins: in0=and_19_out, in1=and_20_out, in2=and_21_out, in3=and_22_out, in4=and_23_out, out=open
  // OR_Gate or_8 has open pins: in0=and_24_out, in1=and_25_out, in2=and_26_out, in3=and_27_out, in4=and_28_out, out=open
  LED led_6 (.in(not_1_out));
  LED led_7 (.in(or_9_out));
  or or_9 (or_9_out, and_29_out, and_30_out);
  LED led_8 (.in(or_10_out));
  or or_10 (or_10_out, and_31_out, and_32_out, and_33_out);
  or or_11 (or_11_out, and_34_out, and_35_out, and_36_out, and_37_out);
  LED led_9 (.in(or_11_out));
  LED led_10 (.in(or_12_out));
  or or_12 (or_12_out, and_38_out, and_39_out, and_40_out);

  // Notes on the sheet:
  //   4 3 2 1 0순서 입니다
  //   a rotor
  //   b rotor
  //   c rotor
  //   완전하진 않지만 일단 완성해봤습니다.
endmodule
